# Fritzing sketch RGB_gesture_sensor_scheme (saved by Fritzing 0.9.3b)

parts:
  Part1 = Arduino Uno (Rev3)
  R1 = Resistor [tolerance=±5% resistance=220 package=THT]
  R3 = Resistor [tolerance=±5% resistance=220 package=THT]
  R2 = Resistor [tolerance=±5% resistance=220 package=THT]
  RGB_LED = RGB LED (com. anode, rbg) [package="5 mm [THT]"]
  PART1 = APDS-9960 RGB and Gesture Sensor [part_number=SEN-12787]

nets:
  N1: Part1.A4/SDA, PART1.SDA
  N2: Part1.A5/SCL, PART1.SCL
  GND: Part1.GND, RGB_LED.common_anode, PART1.GND
  N3: Part1.D2, PART1.INT
  N4: Part1.D3_PWM, R3.Pin_0
  N5: Part1.D5_PWM, R2.Pin_0
  N6: Part1.D6_PWM, R1.Pin_0
  3V3: Part1.3V3, PART1.VCC
  N7: R1.Pin_1, RGB_LED.green_cathode
  N8: R3.Pin_1, RGB_LED.red_cathode
  N9: R2.Pin_1, RGB_LED.blue_cathode

custom parts:
  APDS-9960 RGB and Gesture Sensor: Breakout board for the Avago APDS-9960 proximity, light, RGB, and gesture sensors. Please visit www.sparkfun.com to learn more.

// code stored in the sketch: Untitled.ino

